# Fritzing sketch Arduino Dual LFO (saved by Fritzing 0.9.3b)
circuit board: 14.9013cm x 7.84578cm
breadboards: 1

parts:
  R1 = Resistor [tolerance=±5% resistance=1k part_number="Lowpass (2)" package=THT]
  C1 = Ceramic Capacitor [capacitance=100nF package="100 mil [THT, multilayer]"]
  C2 = Ceramic Capacitor [capacitance=100nF package="100 mil [THT, multilayer]"]
  S5 = Round Pushbutton [part_number="Wave (1)"]
  LED2 = LED - 5mm [color="Red (633nm)" part_number=(0) package="5 mm [THT]"]
  R4 = Resistor [tolerance=±5% resistance=1k package=THT]
  R5 = Resistor [tolerance=±5% resistance=1k package=THT]
  S6 = Round Pushbutton [part_number="Wave (2)"]
  S7 = Round Pushbutton [part_number="Mode Switch"]
  LED3 = LED - 5mm [color="Red (633nm)" part_number=(1) package="5 mm [THT]"]
  R2 = Resistor [tolerance=±5% resistance=1k part_number="Lowpass (1)" package=THT]
  R8 = Rotary Potentiometer (Small) [maximum_resistance=10kΩ package=THT]
  R7 = Rotary Potentiometer (Small) [maximum_resistance=10kΩ package=THT]
  R6 = Rotary Potentiometer (Small) [maximum_resistance=10kΩ package=THT]
  R9 = Rotary Potentiometer (Small) [maximum_resistance=10kΩ package=THT]
  part = Rotary Potentiometer (Small) [maximum_resistance=100kΩ package=THT]  # not connected
  Part1 = Arduino Uno (Rev3)

nets:
  PWM Output (2): R1.Pin_0, Part1.D11_PWM/MOSI
  LFO (2): R1.Pin_1, C1.0
  GND/Mode Switch: C1.1, C2.1, S5.leg1, R4.Pin_1, R5.Pin_1, S6.leg1, S7.leg0, S7.leg1, R8.leg1, R7.leg1, R6.leg1, R9.leg1, Part1.D9_PWM, Part1.GND
  LFO (1): C2.0, R2.Pin_1
  Wave Switch (1): S5.leg0, Part1.D10_PWM/SS
  N1: LED2.cathode, R4.Pin_0
  LED Bar 0: LED2.anode, Part1.D7
  N2: R5.Pin_0, LED3.cathode
  Wave Switch (2): S6.leg0, Part1.D12/MISO
  LED Bar 1: LED3.anode, Part1.D8
  PWM Output (1): R2.Pin_0, Part1.D3_PWM
  Frequency (2): R8.wiper, Part1.A1
  5V: R8.leg2, R7.leg2, R6.leg2, R9.leg2, Part1.5V
  Depth (1): R7.wiper, Part1.A4/SDA
  Frequency (1): R6.wiper, Part1.A0
  Depth (2): R9.wiper, Part1.A5/SCL
  Trigger: Part1.D6_PWM

notes:
  LFO 1 & 2 OUT :
  MODE SWITCH
  LFO (1)
  WAVEFORM SELECTOR SWITCH
  FREQUENCY POT
  DEPT POT
  LFO (2)
  WAVEFORM SELECTOR SWITCH
  FREQUENCY POT
  DEPT POT
  LED BAR
